# Fritzing sketch cp 29 (saved by Fritzing 0.9.3b)
breadboards: 1

parts:
  U1 = 74HC595 [package="DIP16 [THT]"]  # not connected
  Part1 = Arduino Uno (Rev3)
  S1 = Pushbutton [package="[THT]"]
  7_Segment = 7-Segment LED Display [package=THT]
  R1 = Resistor [tolerance=±5% resistance=220 package=THT]  # not connected
  R2 = Resistor [tolerance=±5% resistance=220 package=THT]  # not connected
  R3 = Resistor [tolerance=±5% resistance=220 package=THT]  # not connected
  R4 = Resistor [tolerance=±5% resistance=220 package=THT]  # not connected
  R5 = Resistor [tolerance=±5% resistance=220 package=THT]  # not connected
  R6 = Resistor [tolerance=±5% resistance=220 package=THT]  # not connected
  R7 = Resistor [tolerance=±5% resistance=220 package=THT]  # not connected
  R8 = Resistor [tolerance=±5% resistance=220 package=THT]  # not connected

nets:
  N1: Part1.D2, S1.Pin_3, S1.Pin_4
  N2: Part1.5V, S1.Pin_1, S1.Pin_2
  N3: Part1.GND, 7_Segment.commAnode#2
