# Fritzing sketch Opbygning af selvkørende bil, uno (saved by Fritzing 0.9.3b)
circuit board: 8.46667cm x 5.64444cm
breadboards: 1

parts:
  M3 = Hobby Gearmotor with 48:1 gearbox [part_number=ROB-13302]
  S1 = H-Bridge with L298N
  M4 = Hobby Gearmotor with 48:1 gearbox [part_number=ROB-13302]
  U1 = mystery part, 3 pins [chip_label="IR line tracker"]
  U2 = mystery part, 3 pins [chip_label="IR line tracker"]
  U3 = mystery part, 3 pins [chip_label="IR line tracker"]
  U4 = mystery part, 4 pins [chip_label="Speed Sensor Double Slot type Optocoupler"]
  Part1 = Arduino Uno (Rev3) - ICSP
  VCC2 = Battery block 9V  # not connected
  BAT1 = Battery Holders [package=battery-aa]
  R2 = Resistor [tolerance=±5% resistance=220 package=THT]
  R3 = Resistor [tolerance=±5% resistance=220 package=THT]
  R1 = Resistor [tolerance=±5% resistance=220 package=THT]
  R4 = Resistor [tolerance=±5% resistance=1k package=THT]
  U5 = Mystery Part - 4 pins [chip_label="Speed Sensor Double Slot type Optocoupler" package=THT]
  BAT3 = Battery Holders [package=battery-aa]
  BAT4 = Battery Holders [package=battery-aa]
  BAT5 = Battery Holders [package=battery-aa]
  BAT6 = Battery Holders [package=battery-aa]
  BAT7 = Battery Holders [package=battery-aa]

nets (from the breadboard view):
  N1: M3.pin_1, S1.M2-02
  N2: M3.pin_2, S1.M2-01
  N3: S1.12V, BAT7.-
  GND: S1.GND, U1.pin2, U2.pin2, U3.pin2, U4.pin2, Part1.GND, BAT1.+, R2.Pin_0, R3.Pin_0, R1.Pin_0, U5.gnd
  5V: S1.5V, U4.pin1, Part1.5V, R4.Pin_0, U5.vin
  N4: S1.ENA, Part1.D11_PWM/MOSI
  N5: S1.IN1, Part1.D13/SCK
  N6: S1.IN2, Part1.D12/MISO
  N7: S1.IN3, Part1.D9_PWM
  N8: S1.IN4, Part1.D8
  N9: S1.ENB, Part1.D10_PWM/SS
  N10: S1.M1-01, M4.pin_1
  N11: S1.M1-02, M4.pin_2
  N12: U1.pin1, U2.pin1, U3.pin1, R4.Pin_1
  N13: U1.pin3, Part1.D4, R2.Pin_1
  N14: U2.pin3, Part1.D6_PWM, R1.Pin_1
  N15: U3.pin3, Part1.D5_PWM, R3.Pin_1
  N16: U4.pin3, Part1.D2
  N17: Part1.D3_PWM, U5.D0
  N18: BAT1.-, BAT3.+
  N19: BAT3.-, BAT4.+
  N20: BAT4.-, BAT5.+
  N21: BAT5.-, BAT6.+
  N22: BAT6.-, BAT7.+

custom parts:
  H-Bridge with L298N: h-bridge
  Mystery Part - 4 pins: A dummy, proxy, ersatz, stand-in part for whatever you want. With 4 pins on a 100 mil inline pin header footprint.

// code stored in the sketch: motorcontroller_stepcounter_linetracker.ino
void setup() {
}
