# Fritzing sketch build (saved by Fritzing 0.9.3b)

parts:
  Part1 = Arduino Uno (Rev3)
  KY-1 = Keyes Relay [package=THT]
  D2F1 = D2F-FL Omron Snap Action Limit Switch with Level

nets:
  N1: Part1.D2, KY-1.signal
  N2: Part1.5V, KY-1.power
  N3: Part1.GND, KY-1.ground
  N4: KY-1.C, D2F1.NO
  N5: KY-1.NO, D2F1.NC

custom parts:
  Keyes Relay: The Keyes 5V relay module is suitable for SCM development, home appliance control. It uses a 5V~12V TIL control signal which can control DC / AC signal.
  D2F-FL Omron Snap Action Limit Switch with Level: Snap action switch with stainless steel lever.

// code stored in the sketch: build.ino
void setup() {
  // put your setup code here, to run once:
  pinMode (13,OUTPUT);
}

void loop() {
  // put your main code here, to run repeatedly:
  digitalWrite(13,HIGH);
  delay(100);
  digitalWrite(13,LOW);
  delay(100);
}
