# Fritzing sketch alphacharlies design (saved by Fritzing 0.9.3b)
circuit board: 8.46667cm x 5.64444cm
breadboards: 1

parts:
  D1 = LTE-302 [package=lte-302]
  Q2 = LTR-301 [package=ltr-301]
  U1 = POT [package=pot_mammoth]
  Q3 = NPN-Transistor [package="TO92 [THT]"]
  R1 = Resistor [tolerance=±5% resistance=470 package=THT]
  D3 = LTE-302 [package=lte-302]
  Q4 = LTR-301 [package=ltr-301]
  U2 = POT [package=pot_mammoth]
  Q5 = NPN-Transistor [package="TO92 [THT]"]
  R3 = Resistor [tolerance=±5% resistance=470 package=THT]
  R4 = Resistor [tolerance=±5% resistance=10k package=THT]
  R2 = Resistor [tolerance=±5% resistance=10k package=THT]
  D4 = Rectifier Diode [part_number=1N4001 package="300 mil [THT]"]
  D5 = Rectifier Diode [part_number=1N4001 package="300 mil [THT]"]
  Part1 = Arduino Uno (Rev3)

nets:
  N1: D1.A, R1.Pin_0
  N2: D1.C, Q2.E, D3.C, Q4.E, R4.Pin_1, R2.Pin_1, D4.cathode, D5.cathode, Part1.GND
  N3: Q2.C, U1.A, Q3.B
  N4: U1.E, Q3.C, R1.Pin_1, U2.E, Q5.C, R3.Pin_1, Part1.5V
  N5: Q3.E, R2.Pin_0
  N6: D3.A, R3.Pin_0
  N7: Q4.C, U2.A, Q5.B
  N8: Q5.E, R4.Pin_0
  N9: D4.anode, Part1.D6_PWM
  N10: D5.anode, Part1.D5_PWM
