# Fritzing sketch alphacharlies design_3b (saved by Fritzing 0.9.3b)
circuit board: 8.46667cm x 5.64444cm
breadboards: 1

parts:
  Q2 = LTR-301 [package=ltr-301]
  U1 = POT [package=pot_mammoth]
  Q3 = NPN-Transistor [package="TO92 [THT]"]
  R1 = Resistor [tolerance=±5% resistance=470 package=THT]
  D3 = LTE-302 [package=lte-302]
  Q4 = LTR-301 [package=ltr-301]
  U2 = POT [package=pot_mammoth]
  Q5 = NPN-Transistor [package="TO92 [THT]"]
  R3 = Resistor [tolerance=±5% resistance=470 package=THT]
  R4 = Resistor [tolerance=±5% resistance=10k package=THT]
  R2 = Resistor [tolerance=±5% resistance=10k package=THT]
  Part1 = Arduino Uno (Rev3)
  D1 = LTE-302 [package=lte-302]
  SCR1 = 2N5064 [package=to-92-kit]
  SCR2 = 2N5064 [package=to-92-kit]

nets:
  N1: Q2.C, U1.A, Q3.B
  N2: Q2.E, D3.C, Q4.E, Part1.GND, D1.C, SCR1.Cathode, SCR2.Cathode
  N3: U1.E, Q3.C, R1.Pin_1, U2.E, Q5.C, R3.Pin_1, Part1.5V
  N4: Q3.E, R2.Pin_0
  N5: R1.Pin_0, D1.A
  N6: D3.A, R3.Pin_0
  N7: Q4.C, U2.A, Q5.B
  N8: Q5.E, R4.Pin_0
  N9: R4.Pin_1, SCR2.Gate
  N10: R2.Pin_1, SCR1.Gate
  N11: Part1.D5_PWM, SCR2.Anode
  N12: Part1.D6_PWM, SCR1.Anode

custom parts:
  2N5064: SCR 200V 800mA Sensitive Gate Through Hole TO-92
