# Fritzing sketch gerdin (saved by Fritzing 0.9.3b)
breadboards: 1

parts:
  Part1 = Arduino Uno (Rev3)
  S1 = Pushbutton [package="[THT]"]
  S2 = Pushbutton [package="[THT]"]
  S3 = Pushbutton [package="[THT]"]
  S4 = Pushbutton [package="[THT]"]
  S5 = Pushbutton [package="[THT]"]
  R1 = Resistor [tolerance=±5% resistance=10k package=THT]
  R3 = Resistor [tolerance=±5% resistance=10k package=THT]
  R4 = Resistor [tolerance=±5% resistance=10k package=THT]
  R5 = Resistor [tolerance=±5% resistance=10k package=THT]
  R6 = Resistor [tolerance=±5% resistance=10k package=THT]
  LCD1 = LCD screen
  R7 = Photocell (LDR) [package=THT]
  MOTOR1 = 28BYJ-48 Stepper Motor
  LCM1602_IIC1 = LCM1602 IIC [part_number="LCM1602 IIC" chip_label="LCM1602 IIC" package="DIP (Dual Inline) [THT]"]
  BREAKOUT1 = ULN2003A breakout board
  R8 = Resistor [tolerance=±5% resistance=220 package=THT]
  VCC1 = 4 x AAA Battery Mount

nets:
  N1: Part1.A0, R7.pin_0, R8.Pin_1
  N2: Part1.A4/SDA, LCM1602_IIC1.SDA
  N3: Part1.A5/SCL, LCM1602_IIC1.SCL
  N4: Part1.D8, S4.Pin_3, S4.Pin_4, R6.Pin_1
  N5: Part1.D9_PWM, S5.Pin_3, S5.Pin_4, R3.Pin_1
  N6: Part1.D10_PWM/SS, BREAKOUT1.In_1
  N7: Part1.D11_PWM/MOSI, BREAKOUT1.In_2
  N8: Part1.D12/MISO, BREAKOUT1.In_3
  N9: Part1.D13/SCK, BREAKOUT1.In_4
  N10: Part1.D5_PWM, S1.Pin_3, S1.Pin_4, R1.Pin_1
  N11: Part1.D6_PWM, S2.Pin_3, S2.Pin_4, R4.Pin_1
  N12: Part1.D7, S3.Pin_3, S3.Pin_4, R5.Pin_1
  5V: Part1.5V, S1.Pin_1, S1.Pin_2, S2.Pin_1, S2.Pin_2, S3.Pin_1, S3.Pin_2, S4.Pin_1, S4.Pin_2, S5.Pin_1, S5.Pin_2, R7.pin_1, LCM1602_IIC1.VCC
  GND: Part1.GND, R3.Pin_0, R4.Pin_0, R5.Pin_0, R6.Pin_0, LCM1602_IIC1.GND, R8.Pin_0
  VSS: LCD1.VSS, LCM1602_IIC1.VSS
  VDD: LCD1.VDD, LCM1602_IIC1.VDD
  N13: LCD1.V0, LCM1602_IIC1.V0
  N14: LCD1.RS, LCM1602_IIC1.RS
  N15: LCD1.R/W, LCM1602_IIC1.RW
  N16: LCD1.E, LCM1602_IIC1.E
  N17: LCD1.DB0, LCM1602_IIC1.D0
  N18: LCD1.DB1, LCM1602_IIC1.D1
  N19: LCD1.DB2, LCM1602_IIC1.D2
  N20: LCD1.DB3, LCM1602_IIC1.D3
  N21: LCD1.DB4, LCM1602_IIC1.D4
  N22: LCD1.DB5, LCM1602_IIC1.D5
  N23: LCD1.DB6, LCM1602_IIC1.D6
  N24: LCD1.DB7, LCM1602_IIC1.D7
  N25: LCD1.LED+, LCM1602_IIC1.A
  N26: LCD1.LED-, LCM1602_IIC1.K
  N27: MOTOR1.BLUE, BREAKOUT1.BLUE_wire
  N28: MOTOR1.PINK, BREAKOUT1.PINK_wire
  N29: MOTOR1.RED, BREAKOUT1.RED_wire
  N30: MOTOR1.ORANGE, BREAKOUT1.ORANGE_wire
  N31: MOTOR1.YELLOW, BREAKOUT1.YELLOW_wire
  N32: LCM1602_IIC1.LED_A, LCM1602_IIC1.LED_B
  N33: BREAKOUT1.0V, VCC1.-
  N34: BREAKOUT1.+5V, VCC1.+

custom parts:
  28BYJ-48 Stepper Motor: 28BYJ-48 gear-reduction stepper motor (small)
  LCM1602 IIC: I2C-Module to use a 1602 or 2004 LCD on with the wire.h libory Serial LCD Modul
  ULN2003A breakout board: ULN2003A 7-way Darlington Transistor Driver on breakoutboard
